// Logisim project Lab1.circ as structural Verilog: 3 circuits, main circuit main
module main (
  input  A,
  input  B,
  output S
);

  wire and_1_out, and_2_out;

  and and_1 (and_1_out, ~A, B);  // AND_Gate
  and and_2 (and_2_out, A, ~B);  // AND_Gate
  or or_1 (S, and_1_out, and_2_out);

  // Notes on the sheet:
  //   1-Bit XOR Circuit
endmodule

module onebitadder (
  input  A,
  input  B,
  input  Cin,
  output S,
  output Cout
);

  wire and_1_out, and_2_out, main_1_s;

  main main_1 (.A(A), .B(B), .S(main_1_s));
  and and_1 (and_1_out, A, B);
  and and_2 (and_2_out, Cin, main_1_s);
  or or_1 (Cout, and_1_out, and_2_out);
  main main_2 (.A(main_1_s), .B(Cin), .S(S));

  // Notes on the sheet:
  //   1 Bit Adder
endmodule

module four_bit_adder (
  input  [3:0] A,
  input  [3:0] B,
  input  Cin,
  output Cout,
  output [3:0] S
);

  wire onebitadder_1_cout, onebitadder_2_cout, onebitadder_3_cout;

  onebitadder onebitadder_1 (.A(A[0]), .B(B[0]), .Cin(Cin), .S(S[0]), .Cout(onebitadder_1_cout));
  onebitadder onebitadder_2 (.A(A[1]), .B(B[1]), .Cin(onebitadder_1_cout), .S(S[1]), .Cout(onebitadder_2_cout));
  onebitadder onebitadder_3 (.A(A[2]), .B(B[2]), .Cin(onebitadder_2_cout), .S(S[2]), .Cout(onebitadder_3_cout));
  onebitadder onebitadder_4 (.A(A[3]), .B(B[3]), .Cin(onebitadder_3_cout), .S(S[3]), .Cout(Cout));

  // Notes on the sheet:
  //   4-Bit Adder
endmodule
