// Logisim project ALU_BRL.circ as structural Verilog: 17 circuits, main circuit LeftShift32
module LeftShift32 (
  input  Cin,
  input  [31:0] B,
  input  [4:0] Sa,
  output [31:0] C
);

  wire [31:0] leftshift1_1_c, leftshift2_1_c, leftshift4_1_c, leftshift8_1_c, leftshift16_1_c,
       multiplexer_1_out, multiplexer_2_out, multiplexer_3_out, multiplexer_4_out;

  LeftShift1 leftshift1_1 (.Cin(Cin), .B(B), .C(leftshift1_1_c));
  Multiplexer #(.width(32)) multiplexer_1 (.in0(B), .in1(leftshift1_1_c), .out(multiplexer_1_out), .sel(Sa[0]));
  LeftShift2 leftshift2_1 (.Cin(Cin), .B(multiplexer_1_out), .C(leftshift2_1_c));
  Multiplexer #(.width(32)) multiplexer_2 (
    .in0(multiplexer_1_out), .in1(leftshift2_1_c), .out(multiplexer_2_out), .sel(Sa[1]));
  LeftShift4 leftshift4_1 (.Cin(Cin), .B(multiplexer_2_out), .C(leftshift4_1_c));
  Multiplexer #(.width(32)) multiplexer_3 (
    .in0(multiplexer_2_out), .in1(leftshift4_1_c), .out(multiplexer_3_out), .sel(Sa[2]));
  LeftShift8 leftshift8_1 (.Cin(Cin), .B(multiplexer_3_out), .C(leftshift8_1_c));
  Multiplexer #(.width(32)) multiplexer_4 (
    .in0(multiplexer_3_out), .in1(leftshift8_1_c), .out(multiplexer_4_out), .sel(Sa[3]));
  Multiplexer #(.width(32)) multiplexer_5 (.in0(multiplexer_4_out), .in1(leftshift16_1_c), .out(C), .sel(Sa[4]));
  LeftShift16 leftshift16_1 (.Cin(Cin), .B(multiplexer_4_out), .C(leftshift16_1_c));

  // Notes on the sheet:
  //   32-Bit Left Shifter
endmodule

module Add32 (
  input  [31:0] A,
  input  Cin,
  input  [31:0] B,
  output [31:0] C,
  output V
);

  wire eightbitadd_1_cout, fourbitadd_1_cout, onebitadd_1_cout, onebitadd_2_cout, sixteenbitadd_1_cout,
       twobitadd_1_cout;

  sixteenbitadd sixteenbitadd_1 (.A(A[15:0]), .B(B[15:0]), .C(Cin), .S(C[15:0]), .Cout(sixteenbitadd_1_cout));
  eightbitadd eightbitadd_1 (
    .A(A[23:16]), .B(B[23:16]), .C(sixteenbitadd_1_cout), .S(C[23:16]), .Cout(eightbitadd_1_cout));
  fourbitadd fourbitadd_1 (.A(A[27:24]), .B(B[27:24]), .C(eightbitadd_1_cout), .S(C[27:24]), .Cout(fourbitadd_1_cout));
  twobitadd twobitadd_1 (.A(A[29:28]), .Cin(fourbitadd_1_cout), .B(B[29:28]), .S(C[29:28]), .Cout(twobitadd_1_cout));
  onebitadd onebitadd_1 (.A(A[30]), .B(B[30]), .Cin(twobitadd_1_cout), .S(C[30]), .Cout(onebitadd_1_cout));
  onebitadd onebitadd_2 (.A(A[31]), .B(B[31]), .Cin(onebitadd_1_cout), .S(C[31]), .Cout(onebitadd_2_cout));
  xor xor_1 (V, onebitadd_1_cout, onebitadd_2_cout);

  // Notes on the sheet:
  //   32-Bit Signed Adder
  //   Split 32 bits into indivudal bits so can get the carryIn value of MSB
endmodule

module ALU32 (
  input  [31:0] A,
  input  [31:0] B,
  input  [3:0] Op,
  input  [4:0] Sa,
  output [31:0] C,
  output V
);

  wire add32_1_v, and_1_out, and_2_out, compbitoraddshift_1_c, xor_2_out;
  wire [31:0] add32_1_c, bit_extender_1_out, bitwiseunit_1_c, comparatorunit_1_c, multiplexer_1_out,
       multiplexer_2_out, shift32_1_c, xor_1_out;

  and and_1 (and_1_out, B[31], Op[2], Op[0]);
  assign bit_extender_1_out = {{31{Op[3]}}, Op[3]};  // Bit_Extender bit_extender_1
  assign xor_1_out = B ^ bit_extender_1_out;  // XOR_Gate xor_1, 32 bits wide
  comparatorUnit comparatorunit_1 (.A(A), .B(B), .Op(Op[1:0]), .C(comparatorunit_1_c));
  bitwiseUnit bitwiseunit_1 (.A(A), .B(B), .Op(Op[1:0]), .C(bitwiseunit_1_c));
  Shift32 shift32_1 (.Cin(and_1_out), .B(B), .Sa(Sa), .SL(Op[2]), .C(shift32_1_c));
  Add32 add32_1 (.A(A), .Cin(Op[3]), .B(xor_1_out), .C(add32_1_c), .V(add32_1_v));
  Multiplexer #(.width(32)) multiplexer_1 (
    .in0(comparatorunit_1_c), .in1(bitwiseunit_1_c), .out(multiplexer_1_out), .sel(xor_2_out));
  xor xor_2 (xor_2_out, Op[1], Op[2]);
  Multiplexer #(.width(32)) multiplexer_2 (.in0(shift32_1_c), .in1(add32_1_c), .out(multiplexer_2_out), .sel(Op[1]));
  Multiplexer #(.width(32)) multiplexer_3 (
    .in0(multiplexer_1_out), .in1(multiplexer_2_out), .out(C), .sel(compbitoraddshift_1_c));
  compbitORaddshift compbitoraddshift_1 (.b3(Op[3]), .b2(Op[2]), .b1(Op[1]), .c(compbitoraddshift_1_c));
  and and_2 (and_2_out, Op[1], add32_1_v);
  and and_3 (V, compbitoraddshift_1_c, and_2_out);

  // Notes on the sheet:
  //   If bit3 of Op=1, invert B to subtract & carryIn=1; else add
  //   32-Bit RISC-V ALU
  //   Specific comp/bit Op depends on bit0,bit1
  //   Left/right based on bit2
  //   Arithmetic Right w/ carryIn=1 if MSB=bit2=bit0=1
  //   Choose bw shift or add result based on bit1
  //   Choose b/w comparator or bitwise result based on XOR of bit2,bit1
  //   Choose bw comp/bit and shift/add result
  //   V=1 only if there is overflow AND Op calls for add/sub
  //   See subcircuit for explanation
endmodule

module Shift32 (
  input  Cin,
  input  [31:0] B,
  input  [4:0] Sa,
  input  SL,
  output [31:0] C
);

  wire [31:0] leftshift32_1_c, multiplexer_1_out;

  Multiplexer #(.width(32)) multiplexer_1 (
    .in0(B),
    .in1({B[0], B[1], B[2], B[3], B[4], B[5], B[6], B[7], B[8], B[9], B[10], B[11], B[12], B[13], B[14], B[15], B[16], B[17], B[18], B[19], B[20], B[21], B[22], B[23], B[24], B[25], B[26], B[27], B[28], B[29], B[30], B[31]}),
    .out(multiplexer_1_out), .sel(SL));
  LeftShift32 leftshift32_1 (.Cin(Cin), .B(multiplexer_1_out), .Sa(Sa), .C(leftshift32_1_c));
  Multiplexer #(.width(32)) multiplexer_2 (
    .in0(leftshift32_1_c),
    .in1({leftshift32_1_c[0], leftshift32_1_c[1], leftshift32_1_c[2], leftshift32_1_c[3], leftshift32_1_c[4], leftshift32_1_c[5], leftshift32_1_c[6], leftshift32_1_c[7], leftshift32_1_c[8], leftshift32_1_c[9], leftshift32_1_c[10], leftshift32_1_c[11], leftshift32_1_c[12], leftshift32_1_c[13], leftshift32_1_c[14], leftshift32_1_c[15], leftshift32_1_c[16], leftshift32_1_c[17], leftshift32_1_c[18], leftshift32_1_c[19], leftshift32_1_c[20], leftshift32_1_c[21], leftshift32_1_c[22], leftshift32_1_c[23], leftshift32_1_c[24], leftshift32_1_c[25], leftshift32_1_c[26], leftshift32_1_c[27], leftshift32_1_c[28], leftshift32_1_c[29], leftshift32_1_c[30], leftshift32_1_c[31]}),
    .out(C), .sel(SL));

  // Notes on the sheet:
  //   Right Shift when SL=1
  //   Left Shift when SL=0
  //   Cin denotes bit value used to fill in shifted bits
  //   For rightshift, reverse bits of B before and after leftshift
  //   32-Bit Shifter
  //   Muxes for choosing between left/right shift based on SL value
endmodule

module onebitadd (
  input  A,
  input  B,
  input  Cin,
  output S,
  output Cout
);

  wire and_1_out, and_2_out, xor_1_out;

  and and_1 (and_1_out, A, B);
  xor xor_1 (xor_1_out, A, B);
  xor xor_2 (S, xor_1_out, Cin);
  and and_2 (and_2_out, xor_1_out, Cin);
  or or_1 (Cout, and_1_out, and_2_out);

  // Notes on the sheet:
  //   1-bit Adder
endmodule

module fourbitadd (
  input  [3:0] A,
  input  [3:0] B,
  input  C,
  output [3:0] S,
  output Cout
);

  wire twobitadd_1_cout;

  twobitadd twobitadd_1 (.A(A[1:0]), .Cin(C), .B(B[1:0]), .S(S[1:0]), .Cout(twobitadd_1_cout));
  twobitadd twobitadd_2 (.A(A[3:2]), .Cin(twobitadd_1_cout), .B(B[3:2]), .S(S[3:2]), .Cout(Cout));

  // Notes on the sheet:
  //   4-bit Signed two's Complement Adder
endmodule

module twobitadd (
  input  [1:0] A,
  input  Cin,
  input  [1:0] B,
  output [1:0] S,
  output Cout
);

  wire onebitadd_1_cout;

  onebitadd onebitadd_1 (.A(A[0]), .B(B[0]), .Cin(Cin), .S(S[0]), .Cout(onebitadd_1_cout));
  onebitadd onebitadd_2 (.A(A[1]), .B(B[1]), .Cin(onebitadd_1_cout), .S(S[1]), .Cout(Cout));

  // Notes on the sheet:
  //   2-bit Signed two's Complement Adder
endmodule

module eightbitadd (
  input  [7:0] A,
  input  [7:0] B,
  input  C,
  output [7:0] S,
  output Cout
);

  wire fourbitadd_1_cout;

  fourbitadd fourbitadd_1 (.A(A[3:0]), .B(B[3:0]), .C(C), .S(S[3:0]), .Cout(fourbitadd_1_cout));
  fourbitadd fourbitadd_2 (.A(A[7:4]), .B(B[7:4]), .C(fourbitadd_1_cout), .S(S[7:4]), .Cout(Cout));

  // Notes on the sheet:
  //   8-bit Signed two's Complement Adder
endmodule

module sixteenbitadd (
  input  [15:0] A,
  input  [15:0] B,
  input  C,
  output [15:0] S,
  output Cout
);

  wire eightbitadd_1_cout;

  eightbitadd eightbitadd_1 (.A(A[7:0]), .B(B[7:0]), .C(C), .S(S[7:0]), .Cout(eightbitadd_1_cout));
  eightbitadd eightbitadd_2 (.A(A[15:8]), .B(B[15:8]), .C(eightbitadd_1_cout), .S(S[15:8]), .Cout(Cout));

  // Notes on the sheet:
  //   16-bit Signed two's Complement Adder
endmodule

module LeftShift1 (
  input  Cin,
  input  [31:0] B,
  output [31:0] C
);


  assign C = {B[30:0], Cin};

  // Notes on the sheet:
  //   1-bit Left Shifter
endmodule

module LeftShift2 (
  input  Cin,
  input  [31:0] B,
  output [31:0] C
);


  assign C = {B[29:0], {2{Cin}}};

  // Notes on the sheet:
  //   2-bit left Shifter
endmodule

module LeftShift4 (
  input  Cin,
  input  [31:0] B,
  output [31:0] C
);


  assign C = {B[27:0], {4{Cin}}};

  // Notes on the sheet:
  //   4-bit Left Shifter
endmodule

module LeftShift8 (
  input  Cin,
  input  [31:0] B,
  output [31:0] C
);


  assign C = {B[23:0], {8{Cin}}};

  // Notes on the sheet:
  //   8-bit Left Shifter
endmodule

module LeftShift16 (
  input  Cin,
  input  [31:0] B,
  output [31:0] C
);


  assign C = {B[15:0], {16{Cin}}};

  // Notes on the sheet:
  //   16-bit Left Shifter
endmodule

module bitwiseUnit (
  input  [31:0] A,
  input  [31:0] B,
  input  [1:0] Op,
  output [31:0] C
);

  wire [31:0] and_1_out, nor_1_out, or_1_out, xor_1_out;

  assign or_1_out = A | B;  // OR_Gate or_1, 32 bits wide
  assign and_1_out = A & B;  // AND_Gate and_1, 32 bits wide
  assign xor_1_out = A ^ B;  // XOR_Gate xor_1, 32 bits wide
  assign nor_1_out = ~(A | B);  // NOR_Gate nor_1, 32 bits wide
  Multiplexer #(.select(2), .width(32)) multiplexer_1 (
    .in0(or_1_out), .in1(and_1_out), .in2(xor_1_out), .in3(nor_1_out), .out(C), .sel(Op));

  // Notes on the sheet:
  //   32-Bit Bitwise Operator circuit: OR,AND,NOR,XOR
  //   OR: 00
  //   AND: 01
  //   XOR: 10
  //   NOR: 11
endmodule

module comparatorUnit (
  input  [31:0] A,
  input  [31:0] B,
  input  [1:0] Op,
  output [31:0] C
);

  wire and_1_out, and_2_out, multiplexer_1_out, not_2_out, not_3_out, or_1_out, xor_2_out;
  wire [31:0] not_1_out, xor_1_out;

  assign xor_1_out = A ^ B;  // XOR_Gate xor_1, 32 bits wide
  assign not_1_out = ~xor_1_out;  // NOT_Gate not_1, 32 bits wide
  or or_1 (or_1_out, A[0], A[1], A[2], A[3], A[4], A[5], A[6], A[7], A[8], A[9], A[10], A[11], A[12], A[13], A[14], A[15], A[16], A[17], A[18], A[19], A[20], A[21], A[22], A[23], A[24], A[25], A[26], A[27], A[28], A[29], A[30]);
  not not_2 (not_2_out, A[31]);
  and and_1 (and_1_out, or_1_out, not_2_out);
  and and_2 (and_2_out, not_1_out[0], not_1_out[1], not_1_out[2], not_1_out[3], not_1_out[4], not_1_out[5], not_1_out[6], not_1_out[7], not_1_out[8], not_1_out[9], not_1_out[10], not_1_out[11], not_1_out[12], not_1_out[13], not_1_out[14], not_1_out[15], not_1_out[16], not_1_out[17], not_1_out[18], not_1_out[19], not_1_out[20], not_1_out[21], not_1_out[22], not_1_out[23], not_1_out[24], not_1_out[25], not_1_out[26], not_1_out[27], not_1_out[28], not_1_out[29], not_1_out[30], not_1_out[31]);
  Multiplexer multiplexer_1 (.in0(and_2_out), .in1(and_1_out), .out(multiplexer_1_out), .sel(Op[1]));
  xor xor_2 (xor_2_out, multiplexer_1_out, Op[0]);
  not not_3 (not_3_out, xor_2_out);
  assign C = {{31{1'b0}}, not_3_out};  // Bit_Extender bit_extender_1

  // Notes on the sheet:
  //   ne: 00, eq:01, le:10, gt: 11
  //   given op bit1=1, do gt if bit0=1, le if bit0=0
  //   32-bit Comparator circuit: Equal, not equal, less than or equal to 0, greater than 0
  //   given bit1=0, do eq if bit0=1, ne if bit0=0
  //   If bit1=0 choose eq/ne; if bit1=1, choose gt/le
  //   if bit0=0, flip eq to ne or gt to le
endmodule

module compbitORaddshift (
  input  b3,
  input  b2,
  input  b1,
  output c
);

  wire and_1_out, and_2_out, and_3_out, not_1_out, not_2_out, not_3_out;

  not not_1 (not_1_out, b3);
  not not_2 (not_2_out, b2);
  not not_3 (not_3_out, b1);
  and and_1 (and_1_out, b3, not_3_out);
  and and_2 (and_2_out, b3, not_2_out, b1);
  and and_3 (and_3_out, not_1_out, b2, b1);
  or or_1 (c, and_1_out, and_2_out, and_3_out);

  // Notes on the sheet:
  //   3bit circuit to choose bw AddSub/Shift & Comparator/Bitwise subcircuits
  //   c=a!c + a!bc + !abc
endmodule
