// Logisim project lab3.circ as structural Verilog: 2 circuits, main circuit main
module main (
  input  [3:0] A
);

  wire leddecoder_1_bottom, leddecoder_1_bottomleft, leddecoder_1_bottomright, leddecoder_1_middle,
       leddecoder_1_top, leddecoder_1_topleft, leddecoder_1_topright;

  leddecoder leddecoder_1 (
    .bit3(A[3]), .bit2(A[2]), .bit1(A[1]), .bit0(A[0]), .top(leddecoder_1_top), .bottom(leddecoder_1_bottom),
    .topright(leddecoder_1_topright), .topleft(leddecoder_1_topleft), .bottomright(leddecoder_1_bottomright),
    .bottomleft(leddecoder_1_bottomleft), .middle(leddecoder_1_middle));
  _7_Segment_Display u_7_segment_display_1 (
    .g(leddecoder_1_middle), .f(leddecoder_1_topleft), .a(leddecoder_1_top), .b(leddecoder_1_topright),
    .e(leddecoder_1_bottomleft), .d(leddecoder_1_bottom), .c(leddecoder_1_bottomright));  // open: dp
endmodule

module leddecoder (
  input  bit3,
  input  bit2,
  input  bit1,
  input  bit0,
  output top,
  output bottom,
  output topright,
  output topleft,
  output bottomright,
  output bottomleft,
  output middle
);

  wire and_1_out, and_2_out, and_3_out, and_4_out, and_5_out, and_6_out, and_7_out, and_8_out, and_9_out,
       and_10_out, and_11_out, and_12_out, and_13_out, and_14_out, and_15_out, and_16_out, not_1_out,
       not_2_out, not_3_out;

  not not_1 (not_1_out, bit2);
  not not_2 (not_2_out, bit1);
  not not_3 (not_3_out, bit0);
  and and_1 (and_1_out, not_1_out, not_3_out);
  and and_2 (and_2_out, bit2, bit0);
  and and_3 (and_3_out, not_1_out, not_3_out);
  and and_4 (and_4_out, not_1_out, bit1);
  and and_5 (and_5_out, bit1, not_3_out);
  and and_6 (and_6_out, bit2, not_2_out, bit0);
  and and_7 (and_7_out, not_2_out, not_3_out);
  and and_8 (and_8_out, bit1, bit0);
  and and_9 (and_9_out, not_2_out, not_3_out);
  and and_10 (and_10_out, bit2, not_2_out);
  and and_11 (and_11_out, bit2, not_3_out);
  or or_1 (bottomright, not_2_out, bit0, bit2);
  and and_12 (and_12_out, not_1_out, not_3_out);
  and and_13 (and_13_out, bit1, not_3_out);
  and and_14 (and_14_out, not_1_out, bit1, bit0);
  and and_15 (and_15_out, bit2, not_2_out);
  and and_16 (and_16_out, bit2, not_3_out);
  or or_2 (top, and_1_out, bit1, and_2_out, bit3);
  or or_3 (bottom, and_3_out, and_4_out, and_5_out, and_6_out, bit3);
  or or_4 (topright, not_1_out, and_7_out, and_8_out);
  or or_5 (topleft, and_9_out, and_10_out, and_11_out, bit3);
  or or_6 (bottomleft, and_12_out, and_13_out);
  or or_7 (middle, and_14_out, and_15_out, and_16_out, bit3);
endmodule
