// Logisim project lab4.circ as structural Verilog: 2 circuits, main circuit main
module main (
  input  Inp,
  output Z
);

  wire clock_1_out;
  wire [1:0] comblogic_1_n0, register_1_q;

  Register #(.width(2)) register_1 (.D(comblogic_1_n0), .clk(clock_1_out), .Q(register_1_q));  // open: en, clr
  Clock clock_1 (.out(clock_1_out));
  comblogic comblogic_1 (
    .S0(register_1_q[0]), .S1(register_1_q[1]), .inp(Inp), .Z(Z), .N0(comblogic_1_n0[0]),
    .N1(comblogic_1_n0[1]));
endmodule

module comblogic (
  input  S0,
  input  S1,
  input  inp,
  output Z,
  output N0,
  output N1
);

  wire not_1_out;

  and and_1 (Z, S1, inp);
  not not_1 (not_1_out, inp);
  and and_2 (N1, not_1_out, S0);

  assign N0 = inp;
endmodule
