// Logisim project leftshift32_template.circ as structural Verilog: 6 circuits, main circuit LeftShift32
module LeftShift32 (
  input  Cin,
  input  [31:0] B,
  input  [4:0] Sa,
  output [31:0] C
);

  wire [31:0] eightbitshift_1_c, fourbitshift_1_c, multiplexer_1_out, multiplexer_2_out, multiplexer_3_out,
       multiplexer_4_out, onebitshifter_1_c, sixteenbitshift_1_c, twobitshift_1_c;

  onebitshifter onebitshifter_1 (.Cin(Cin), .B(B), .C(onebitshifter_1_c));
  Multiplexer #(.width(32)) multiplexer_1 (.in0(B), .in1(onebitshifter_1_c), .out(multiplexer_1_out), .sel(Sa[0]));
  twobitshift twobitshift_1 (.Cin(Cin), .B(multiplexer_1_out), .C(twobitshift_1_c));
  Multiplexer #(.width(32)) multiplexer_2 (
    .in0(multiplexer_1_out), .in1(twobitshift_1_c), .out(multiplexer_2_out), .sel(Sa[1]));
  fourbitshift fourbitshift_1 (.Cin(Cin), .B(multiplexer_2_out), .C(fourbitshift_1_c));
  Multiplexer #(.width(32)) multiplexer_3 (
    .in0(multiplexer_2_out), .in1(fourbitshift_1_c), .out(multiplexer_3_out), .sel(Sa[2]));
  eightbitshift eightbitshift_1 (.Cin(Cin), .B(multiplexer_3_out), .C(eightbitshift_1_c));
  Multiplexer #(.width(32)) multiplexer_4 (
    .in0(multiplexer_3_out), .in1(eightbitshift_1_c), .out(multiplexer_4_out), .sel(Sa[3]));
  sixteenbitshift sixteenbitshift_1 (.Cin(Cin), .B(multiplexer_4_out), .C(sixteenbitshift_1_c));
  Multiplexer #(.width(32)) multiplexer_5 (.in0(multiplexer_4_out), .in1(sixteenbitshift_1_c), .out(C), .sel(Sa[4]));
endmodule

module onebitshifter (
  input  Cin,
  input  [31:0] B,
  output [31:0] C
);


  assign C = {B[30:0], Cin};
endmodule

module twobitshift (
  input  Cin,
  input  [31:0] B,
  output [31:0] C
);


  assign C = {B[29:0], {2{Cin}}};
endmodule

module fourbitshift (
  input  Cin,
  input  [31:0] B,
  output [31:0] C
);


  assign C = {B[27:0], {4{Cin}}};
endmodule

module eightbitshift (
  input  Cin,
  input  [31:0] B,
  output [31:0] C
);


  assign C = {B[23:0], {8{Cin}}};
endmodule

module sixteenbitshift (
  input  Cin,
  input  [31:0] B,
  output [31:0] C
);


  assign C = {B[15:0], {16{Cin}}};
endmodule
