// Logisim project RISCV.circ as structural Verilog: 8 circuits, main circuit RISCV
module RISCV (
);

  wire aluopgen_1_slt, clock_1_out, comparator_black_box_1_p4, insndecoder_1_byteaccess,
       insndecoder_1_loadenable, insndecoder_1_storeenable, not_1_out, or_1_out, or_2_out,
       wordaddrselectbits_1_p3;
  wire [1:0] insndecoder_1_insttype;
  wire [2:0] insndecoder_1_funct3;
  wire [3:0] aluopgen_1_op, wordaddrselectbits_1_p4;
  wire [4:0] alu_1_p4, bit_extender_1_out, insndecoder_1_xa, insndecoder_1_xb, insndecoder_1_xw,
       registerfile_1_p8;
  wire [6:0] insndecoder_1_funt7, insndecoder_1_opcode;
  wire [31:0] alu_1_p5, bit_extender_2_out, correctlbbits_1_out32, correctsbbits_1_alignedbits,
       incrementer_1_p3, insndecoder_1_imm, multiplexer_1_out, multiplexer_2_out, multiplexer_4_out,
       multiplexer_5_out, multiplexer_6_out, ram_1_p7, registerfile_1_p1, registerfile_1_p7;
  wire [31:2] incrementer_1_p1;
  wire [31:5] registerfile_1_p8_2;

  // Incrementer #(.width(30)) incrementer_1: pin names not known; wires that end beside it: incrementer_1_p1, incrementer_1_p3[31:2], {incrementer_1_p1, incrementer_1_p3[1:0]}
  Clock clock_1 (.out(clock_1_out));
  Register #(.width(32)) PC (
    .D(incrementer_1_p3), .clk(clock_1_out), .Q({incrementer_1_p1, incrementer_1_p3[1:0]}));  // open: en, clr
  // RISC_VProgramROM risc_vprogramrom_1: pin names not known
  not not_1 (not_1_out, insndecoder_1_insttype[1]);
  insnDecoder insndecoder_1 (
    .Opcode(insndecoder_1_opcode), .imm(insndecoder_1_imm), .xA(insndecoder_1_xa), .xB(insndecoder_1_xb),
    .xW(insndecoder_1_xw), .funct3(insndecoder_1_funct3), .funt7(insndecoder_1_funt7),
    .insttype(insndecoder_1_insttype), .storeEnable(insndecoder_1_storeenable),
    .loadEnable(insndecoder_1_loadenable), .byteAccess(insndecoder_1_byteaccess));  // open: insn
  or or_1 (or_1_out, insndecoder_1_insttype[0], not_1_out);
  // RegisterFile registerfile_1: pin names not known; wires that end beside it: registerfile_1_p1, clock_1_out, or_1_out, insndecoder_1_xw, insndecoder_1_xa, insndecoder_1_xb, registerfile_1_p7, {registerfile_1_p8_2, registerfile_1_p8}
  Multiplexer #(.width(32)) multiplexer_1 (
    .in0(registerfile_1_p7), .in1(insndecoder_1_imm), .out(multiplexer_1_out), .sel(insndecoder_1_opcode[2]));
  Multiplexer #(.width(32)) multiplexer_2 (
    .in0({registerfile_1_p8_2, registerfile_1_p8}), .in1(insndecoder_1_imm), .out(multiplexer_2_out),
    .sel(or_2_out));
  or or_2 (or_2_out, insndecoder_1_insttype[0], insndecoder_1_insttype[1]);
  aluOpGen aluopgen_1 (
    .opcodeB5B4B3({insndecoder_1_opcode[5:4], insndecoder_1_opcode[2]}), .funt3(insndecoder_1_funct3),
    .funt7bit5(insndecoder_1_funt7[5]), .op(aluopgen_1_op), .SLT(aluopgen_1_slt));
  // Comparator_Black_Box comparator_black_box_1: pin names not known; wires that end beside it: registerfile_1_p7, {registerfile_1_p8_2, registerfile_1_p8}, aluopgen_1_slt, comparator_black_box_1_p4
  // ALU alu_1: pin names not known; wires that end beside it: multiplexer_1_out, multiplexer_2_out, aluopgen_1_op, alu_1_p4, alu_1_p5
  Multiplexer #(.width(5)) multiplexer_3 (
    .in0(registerfile_1_p8), .in1(bit_extender_1_out), .out(alu_1_p4), .sel(insndecoder_1_insttype[1]));
  assign bit_extender_1_out = {{1{1'b0}}, {insndecoder_1_opcode[5:4], insndecoder_1_opcode[6], insndecoder_1_opcode[3]}};  // Bit_Extender bit_extender_1
  assign bit_extender_2_out = {{31{1'b0}}, comparator_black_box_1_p4};  // Bit_Extender bit_extender_2
  Multiplexer #(.width(32)) multiplexer_4 (
    .in0(alu_1_p5), .in1(bit_extender_2_out), .out(multiplexer_4_out), .sel(aluopgen_1_slt));
  correctSBBits correctsbbits_1 (
    .Data({registerfile_1_p8_2, registerfile_1_p8}), .selectorBits(wordaddrselectbits_1_p4),
    .alignedBits(correctsbbits_1_alignedbits));
  // wordAddrSelectbits wordaddrselectbits_1: pin names not known; wires that end beside it: alu_1_p5, insndecoder_1_byteaccess, wordaddrselectbits_1_p3, wordaddrselectbits_1_p4
  Multiplexer #(.width(32)) multiplexer_5 (
    .in0(correctsbbits_1_alignedbits), .in1({registerfile_1_p8_2, registerfile_1_p8}),
    .out(multiplexer_5_out), .sel(insndecoder_1_byteaccess));
  correctLBBits correctlbbits_1 (.DOut(ram_1_p7), .selectBits(wordaddrselectbits_1_p4), .out32(correctlbbits_1_out32));
  // RAM ram_1: pin names not known; wires that end beside it: wordaddrselectbits_1_p3, multiplexer_5_out, insndecoder_1_storeenable, wordaddrselectbits_1_p4, clock_1_out, insndecoder_1_loadenable, ram_1_p7
  Multiplexer #(.width(32)) multiplexer_6 (
    .in0(correctlbbits_1_out32), .in1(ram_1_p7), .out(multiplexer_6_out), .sel(insndecoder_1_byteaccess));
  Multiplexer #(.width(32)) multiplexer_7 (
    .in0(multiplexer_6_out), .in1(multiplexer_4_out), .out(registerfile_1_p1), .sel(insndecoder_1_opcode[4]));

  // Notes on the sheet:
  //   Incr bit2
  //   contents of risc_vprogramrom_1 (hex, n*v repeats v):
  //   sb x5, 8(x3) lb x7, 8(x3)
  //   WE =0 when s-type
  //   xA if R/I/S-type, imm if U-type
  //   xB if R-type, imm if I/S-type
  //   xB if R-type, 12 if U-type
  //   ALU result if 0, SLT result if 1
  //   0: choose aligned byte, 1 choose entire 32Bits
  //   0: choose right-aligned byte, 1 choose word
  //   if bit4 Op=0, memory result; if bit4=1, ALU result
endmodule

module immGen (
  input  [31:0] instn,
  output [31:0] imm
);

  wire [31:0] bit_extender_1_out, bit_extender_2_out, bit_extender_3_out;

  assign bit_extender_1_out = {{12{instn[31]}}, instn[31:12]};  // Bit_Extender bit_extender_1
  assign bit_extender_2_out = {{20{instn[31]}}, instn[31:20]};  // Bit_Extender bit_extender_2
  assign bit_extender_3_out = {{20{instn[31]}}, {instn[31:25], instn[11:7]}};  // Bit_Extender bit_extender_3
  Multiplexer #(.select(2), .width(32)) multiplexer_1 (
    .in0(bit_extender_2_out), .in1(bit_extender_2_out), .in2(bit_extender_3_out), .in3(bit_extender_1_out),
    .out(imm), .sel(instn[5:4]));

  // Notes on the sheet:
  //   20 or 12-bit immediate depending on if U or S/I type instruction
  //   Takes 32bit input and outputs correct 32-bit extended immediate value of 
  //   Choose imm based on bit5bit4 OpCode
  //   00,01: 12bit (I); 10: 12bit (S); 11: 20bit (U)
endmodule

module aluOpGen (
  input  [2:0] opcodeB5B4B3,
  input  [2:0] funt3,
  input  funt7bit5,
  output [3:0] op,
  output SLT
);

  wire and_1_out, and_2_out, and_3_out, and_4_out, and_5_out, not_1_out, not_2_out, not_3_out, not_4_out,
       not_5_out;

  not not_1 (not_1_out, opcodeB5B4B3[2]);
  not not_2 (not_2_out, opcodeB5B4B3[0]);
  not not_3 (not_3_out, funt3[2]);
  not not_4 (not_4_out, funt3[0]);
  not not_5 (not_5_out, funt7bit5);
  and and_1 (and_1_out, not_1_out, funt3[2]);
  and and_2 (and_2_out, not_2_out, funt3[2], not_5_out);
  and and_3 (and_3_out, not_2_out, funt3[2]);
  and and_4 (and_4_out, opcodeB5B4B3[2], opcodeB5B4B3[1], not_2_out, funt7bit5);
  and and_5 (and_5_out, opcodeB5B4B3[1], funt3[1]);
  and and_6 (SLT, opcodeB5B4B3[2], opcodeB5B4B3[1], not_2_out, not_3_out, funt3[1], not_4_out, not_5_out);
  or or_1 (op[3], and_1_out, and_2_out);
  or or_2 (op[2], and_3_out, and_4_out);
  or or_3 (op[1], funt3[0], opcodeB5B4B3[0], and_5_out);

  assign op[0] = funt3[0];

  // Notes on the sheet:
  //   Produces Correct ALU Opcode given Bit4,5,4 of instruction Opcode, funct 3, and bit 7 of funct 7, and 1 bit output if SLT is op
endmodule

module insnDecoder (
  input  [31:0] insn,
  output [6:0] Opcode,
  output [31:0] imm,
  output [4:0] xA,
  output [4:0] xB,
  output [4:0] xW,
  output [2:0] funct3,
  output [6:0] funt7,
  output [1:0] insttype,
  output storeEnable,
  output loadEnable,
  output byteAccess
);

  wire not_1_out;

  insnType insntype_1 (.a3({insn[5:4], insn[2]}), .instype(insttype));
  immGen immgen_1 (.instn(insn), .imm(imm));
  and and_1 (storeEnable, insttype[1], not_1_out);
  not not_1 (not_1_out, insttype[0]);
  nor nor_1 (loadEnable, insn[4], insn[5]);

  assign byteAccess = insn[13];
  assign funct3 = insn[14:12];
  assign funt7 = insn[31:25];
  assign Opcode = insn[6:0];
  assign xA = insn[19:15];
  assign xB = insn[24:20];
  assign xW = insn[11:7];

  // Notes on the sheet:
  //   Takes 32 bit instruction and extracts relevant data and instruction type (Opcode, imm, xA, xB, xW, funct3/7)
  //   R: 00, I:01, S:10, U:11
  //   Store if S-type instruction
  //   load if bit4,bit5=0
  //   1 if load/store word, 0 if load/store Byte
endmodule

module insnType (
  input  [2:0] a3,
  output [1:0] instype
);

  wire and_1_out, not_1_out, not_2_out;

  not not_1 (not_1_out, a3[2]);
  not not_2 (not_2_out, a3[1]);
  and and_1 (and_1_out, a3[2], not_2_out);
  or or_1 (instype[0], not_1_out, a3[0]);
  or or_2 (instype[1], a3[0], and_1_out);

  // Notes on the sheet:
  //   Takes bit5, bit4, bit of Opcode to determine Instruction type
  //   R: 00, I:01, S:10, U:11
endmodule

module wordAddrSelectbits (
  input  [31:0] ByteAddress,
  input  wordOrByte,
  output [19:0] WordAddress,
  output [3:0] selectBits
);

  wire not_1_out, not_2_out;
  wire [3:0] and_4_out, bit_extender_1_out;

  not not_1 (not_1_out, ByteAddress[1]);
  not not_2 (not_2_out, ByteAddress[0]);
  and and_1 (and_4_out[3], ByteAddress[1], ByteAddress[0]);
  and and_2 (and_4_out[2], ByteAddress[1], not_2_out);
  and and_3 (and_4_out[1], not_1_out, ByteAddress[0]);
  and and_4 (and_4_out[0], not_1_out, not_2_out);
  Multiplexer #(.width(4)) multiplexer_1 (
    .in0(and_4_out), .in1(bit_extender_1_out), .out(selectBits), .sel(wordOrByte));
  assign bit_extender_1_out = {{3{wordOrByte}}, wordOrByte};  // Bit_Extender bit_extender_1

  assign WordAddress = ByteAddress[21:2];

  // Notes on the sheet:
  //   if 1, access word (1111), if 0, select byte
  //   byte specified by bit0bit1 of ByteAddress:
  //   00: 0001, 01: 0010, 10: 0100, 11: 1000
endmodule

module correctLBBits (
  input  [31:0] DOut,
  input  [3:0] selectBits,
  output [31:0] out32
);

  wire not_1_out, not_2_out, not_3_out;
  wire [1:0] and_2_out;
  wire [7:0] multiplexer_1_out;

  not not_1 (not_1_out, selectBits[2]);
  not not_2 (not_2_out, selectBits[1]);
  not not_3 (not_3_out, selectBits[0]);
  and and_1 (and_2_out[1], not_2_out, not_3_out);
  and and_2 (and_2_out[0], not_1_out, not_3_out);
  Multiplexer #(.select(2), .width(8)) multiplexer_1 (
    .in0(DOut[7:0]), .in1(DOut[15:8]), .in2(DOut[23:16]), .in3(DOut[31:24]), .out(multiplexer_1_out),
    .sel(and_2_out));
  assign out32 = {{24{1'b0}}, multiplexer_1_out};  // Bit_Extender bit_extender_1

  // Notes on the sheet:
  //   Returns proper "right-aligned" 32-bit given selector bits
endmodule

module correctSBBits (
  input  [31:0] Data,
  input  [3:0] selectorBits,
  output [31:0] alignedBits
);

  wire not_1_out, not_2_out, not_3_out;
  wire [1:0] and_2_out;

  not not_1 (not_1_out, selectorBits[2]);
  not not_2 (not_2_out, selectorBits[1]);
  not not_3 (not_3_out, selectorBits[0]);
  and and_1 (and_2_out[1], not_2_out, not_3_out);
  and and_2 (and_2_out[0], not_1_out, not_3_out);
  Multiplexer #(.select(2), .width(32)) multiplexer_1 (
    .in0(Data), .in1({Data[31:16], Data[7:0], Data[15:8]}), .in2({Data[31:24], Data[7:0], Data[23:8]}),
    .in3({Data[7:0], Data[31:8]}), .out(alignedBits), .sel(and_2_out));

  // Notes on the sheet:
  //   Correctly Algins bit0...7 to row based on selectBit for storing bytes
endmodule
